# Fritzing sketch temperature-humidity-data-logger (saved by Fritzing 0.8.7b)
breadboards: 3

parts:
  U1 = NodeMCU V3.0
  DHT1 = DHT22 Humidity and Temperature Sensor
  Nokia_5110_LCD_Module1 = Nokia 5110 LCD basado en PCD8544

nets:
  N1: U1.D0, Nokia_5110_LCD_Module1.RST
  N2: U1.D1, Nokia_5110_LCD_Module1.CE
  N3: U1.D2, Nokia_5110_LCD_Module1.DC
  N4: U1.D3, Nokia_5110_LCD_Module1.DIN
  N5: U1.D4, Nokia_5110_LCD_Module1.CLK
  3V3: U1.3V3, DHT1.VDD, Nokia_5110_LCD_Module1.VCC, Nokia_5110_LCD_Module1.LIGHT
  GND: U1.GND#6, U1.GND#13, U1.GND#16, U1.GND#33, DHT1.GND, Nokia_5110_LCD_Module1.GND
  N6: U1.D5, DHT1.DATA

custom parts:
  NodeMCU V3.0: ESP8266 based NodeMCU
  Nokia 5110 LCD basado en PCD8544: Módulo Nokia 5110 LCD basado en el controlador PCD8544. Versión de 8 pines (sólo entrada).
